// Logisim project hw3_adam.circ as structural Verilog: 5 circuits, main circuit main
module main (
  input  in_1,
  input  in_2,
  output out_3
);

  wire and_1_out, and_2_out, not_1_out, not_2_out;

  not not_1 (not_1_out, in_1);
  not not_2 (not_2_out, in_2);
  and and_1 (and_1_out, not_1_out, in_2);
  and and_2 (and_2_out, in_1, not_2_out);
  or or_1 (out_3, and_1_out, and_2_out);

  // Notes on the sheet:
  //   xor
endmodule

module HalfAdder (
  input  A,
  input  B,
  output sum,
  output carry
);

  wire and_1_out, and_2_out, not_1_out, not_2_out;

  and and_1 (and_1_out, A, not_1_out);
  not not_1 (not_1_out, B);
  and and_2 (and_2_out, B, not_2_out);
  not not_2 (not_2_out, A);
  and and_3 (carry, A, B);
  or or_1 (sum, and_1_out, and_2_out);
endmodule

module FullAdder (
  input  A,
  input  B,
  input  C,
  output sum,
  output carry
);

  wire halfadder_1_carry, halfadder_1_sum, halfadder_2_carry;

  HalfAdder halfadder_1 (.A(A), .B(B), .sum(halfadder_1_sum), .carry(halfadder_1_carry));
  HalfAdder halfadder_2 (.A(halfadder_1_sum), .B(C), .sum(sum), .carry(halfadder_2_carry));
  or or_1 (carry, halfadder_1_carry, halfadder_2_carry);
endmodule

module Adder2 (
  input  [1:0] A,
  input  [1:0] B,
  output [1:0] sum,
  output carry
);

  wire fulladder_1_carry;

  FullAdder fulladder_1 (.A(A[0]), .B(B[0]), .sum(sum[0]), .carry(fulladder_1_carry));  // open: C
  FullAdder fulladder_2 (.A(A[1]), .B(B[1]), .C(fulladder_1_carry), .sum(sum[1]), .carry(carry));
endmodule

module ALU (
  input  [3:0] A,
  input  [3:0] B,
  input  [1:0] SEL,
  output [3:0] RESULT
);

  wire [0:0] comparator_1_eq;
  wire [3:0] adder_1_out, and_1_out;

  Comparator #(.mode("unsigned"), .width(4)) comparator_1 (.a(A), .b(B), .eq(comparator_1_eq[0]));  // open: gt, lt
  Adder #(.width(4)) adder_1 (.a(A), .b(B), .out(adder_1_out));  // open: cin, cout
  assign and_1_out = A & B;  // AND_Gate and_1, 4 bits wide
  Multiplexer #(.select(2), .width(4)) multiplexer_1 (
    .in0(adder_1_out), .in1(and_1_out), .in2(B), .in3({3'b000, comparator_1_eq[0]}), .out(RESULT), .sel(SEL));

  // Notes on the sheet:
  //   0 = add
  //   1 = and
  //   2 = pass through (B)
  //   3 = compare
  //   SEL_0
  //   SEL_1
  //   SEL_2
  //   SEL_3
endmodule
