// Logisim project rs.circ as structural Verilog: 1 circuit, main circuit main
module main (
  input  r,
  input  s,
  output out_3
);

  wire and_1_out, and_2_out, not_1_out, not_2_out;

  not not_1 (not_1_out, r);
  not not_2 (not_2_out, s);
  and and_1 (and_1_out, not_1_out, s);
  and and_2 (and_2_out, r, not_2_out);
  or or_1 (out_3, and_1_out, and_2_out);
endmodule
